# Fritzing sketch AirQuality (saved by Fritzing 1.0.1rc)
circuit board: 9.31497cm x 6.11634cm

parts:
  DS1 = DS18B20 1-Wire Temperature Sensor [part_number=DS18B20]
  Part1 = Arduino Nano (Rev3.0)
  R1 = Resistor [tolerance=±5% power=0.25 resistance=4.7k package=THT]
  Grove1 = Grove OLED 128x96
  Part2 = Adafruit PMSA003I Air Quality Breakout [part_number="Adafruit #4632"]

nets:
  GND: DS1.GND, Part1.GND, Grove1.GND, Part2.GND
  N1: DS1.DQ, Part1.D5
  N2: DS1.VDD, R1.Pin_1
  VCC: Part1.5V, R1.Pin_0, Grove1.VCC, Part2.VCC
  N3: Part1.A5, Grove1.SCL, Part2.SCL
  N4: Part1.A4, Grove1.SDA, Part2.SDA

custom parts:
  Adafruit PMSA003I Air Quality Breakout: Breathe easy, knowing that you can track and sense the quality of the air around you with this Adafruit PMSA003I Air Quality Breakout. This sensor is great for monitoring air quality, in a compact plug-in format. Best of all, unlike almost all other sensors we've seen that are UART interface, this one is I2C interface, which makes it a great match for single board Linux computers like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
